# Fritzing sketch test_VoltageDivider (saved by Fritzing 0.9.3b)
circuit board: 4.4281cm x 1.98687cm
breadboards: 1

parts:
  R1 = Resistor [tolerance=±5% resistance=300 package=THT]
  R2 = Resistor [tolerance=±5% resistance=400 package=THT]
  VCC1 = Battery block 9V
  M1 = DC Motor

nets:
  N1: R1.Pin_0, VCC1.+
  N2: R1.Pin_1, R2.Pin_0, M1.pin_1
  N3: R2.Pin_1, VCC1.-, M1.pin_2
